// Logisim project nano-mips.circ as structural Verilog: 26 circuits, main circuit CPU
module CPU (
);

  wire ARw, clk, DRsrc, DRw, instruction_register_1__10, instruction_register_1__11, IRw, MEMw, PC_plus_plus,
       RFsrc, RFw, RFxy, SRw;
  wire [1:0] instruction_register_1__0, instruction_register_1__2, instruction_register_1__4,
       mux_2_1_2_bits_1_output, mux_2_1_2_bits_2_output;
  wire [3:0] alu_1_output, alu_1_zero, ar_address_register_1_output, dr_data_register_1_output,
       instruction_register_1__9, mux_2_1_4_bits_1_output, mux_2_1_4_bits_2_output,
       pc_programe_counter_register_1_output, ram_1_data, rf_rgister_file_4x4_bits_1_x_output,
       rf_rgister_file_4x4_bits_1_y_output;
  wire [11:0] rom_1_data;

  Clock clock_1 (.out(clk));
  PC_Programe_Counter_Register pc_programe_counter_register_1 (
    .\output (pc_programe_counter_register_1_output), .clk(clk), .count_enable(PC_plus_plus));
  RF_Rgister_File__4x4_bits rf_rgister_file_4x4_bits_1 (
    .Input(mux_2_1_4_bits_2_output), .X_output(rf_rgister_file_4x4_bits_1_x_output), .clk(clk),
    .dst(instruction_register_1__4), .X(mux_2_1_2_bits_1_output), .Y(mux_2_1_2_bits_2_output), .write(RFw),
    .Y_output(rf_rgister_file_4x4_bits_1_y_output));
  ROM #(.addrWidth(4), .dataWidth(12)) rom_1 (
    .addr(pc_programe_counter_register_1_output), .data(rom_1_data));  // open: sel
  Mux_2_1__2_bits mux_2_1_2_bits_1 (
    .Input_0(instruction_register_1__2), .Input_1(instruction_register_1__4),
    .Output(mux_2_1_2_bits_1_output), .Select(RFxy));
  Mux_2_1__2_bits mux_2_1_2_bits_2 (
    .Input_0(instruction_register_1__0), .Input_1(instruction_register_1__2),
    .Output(mux_2_1_2_bits_2_output), .Select(RFxy));
  Instruction_Register instruction_register_1 (
    .\input (rom_1_data), .clk(clk), .Write(IRw), ._0(instruction_register_1__0[0]),
    ._1(instruction_register_1__0[1]), ._3(instruction_register_1__2[1]), ._2(instruction_register_1__2[0]),
    ._7(instruction_register_1__9[1]), ._6(instruction_register_1__9[0]), ._5(instruction_register_1__4[1]),
    ._4(instruction_register_1__4[0]), ._11(instruction_register_1__11), ._10(instruction_register_1__10),
    ._9(instruction_register_1__9[3]), ._8(instruction_register_1__9[2]));
  ALU alu_1 (
    .A(rf_rgister_file_4x4_bits_1_x_output), .B(rf_rgister_file_4x4_bits_1_y_output), .Output(alu_1_output),
    .zero(alu_1_zero[0]), .negative(alu_1_zero[1]), .overflow(alu_1_zero[2]), .carry(alu_1_zero[3]),
    .Functions(instruction_register_1__9[2:0]));
  UCC ucc_1 (
    .clk(clk), .MEMw(MEMw), .DRw_2(DRw), .SRw(SRw), .DRsrc(DRsrc), .PC_plus_plus(PC_plus_plus), .IRw(IRw),
    .ARw(ARw), .RFxy(RFxy), .RFsrc(RFsrc), .CodeOp(instruction_register_1__9),
    .M(instruction_register_1__11), .DRw(RFw));
  Mux_2_1__4_bits mux_2_1_4_bits_1 (
    .Input_0(rf_rgister_file_4x4_bits_1_x_output), .Input_1(ram_1_data), .Output(mux_2_1_4_bits_1_output),
    .Select(DRsrc));
  SR_Status_Register sr_status_register_1 (.\input (alu_1_zero), .clk(clk), .Write(SRw));  // open: output
  AR_Address_Register ar_address_register_1 (
    .\input ({instruction_register_1__2, instruction_register_1__0}),
    .\output (ar_address_register_1_output), .clk(clk), .Write(ARw));
  DR_Data_Register dr_data_register_1 (
    .\input (mux_2_1_4_bits_1_output), .\output (dr_data_register_1_output), .clk(clk), .Write(DRw));
  Mux_2_1__4_bits mux_2_1_4_bits_2 (
    .Input_0(dr_data_register_1_output), .Input_1(alu_1_output), .Output(mux_2_1_4_bits_2_output),
    .Select(RFsrc));
  RAM #(.addrWidth(4), .dataWidth(4), .bus("separate")) ram_1 (
    .addr(ar_address_register_1_output), .din(dr_data_register_1_output), .data(ram_1_data), .str(MEMw),
    .clk(clk), .ld(1'b1));  // open: sel, clr

  // Notes on the sheet:
  //   PGM ROM
  //   contents of rom_1 (hex, n*v repeats v):
  //   6 71 ac c1 518 54c 594 5ec a05 a75
  //   DATA RAM
endmodule

module UCC (
  input  clk,
  input  M,
  input  [3:0] CodeOp,
  output DRw,
  output DRsrc,
  output IRw,
  output DRw_2,
  output MEMw,
  output RFxy,
  output RFsrc,
  output PC_plus_plus,
  output ARw,
  output SRw
);

  wire car_control_address_register_1_p3, csr_control_signals_register_1_br,
       csr_control_signals_register_1_cd, not_1_out;
  wire [4:0] car_control_address_register_1_p4, csr_control_signals_register_1_ad0, mapper_1_control_address,
       mux_2_1_5_bits_1_output;
  wire [16:0] rom_1_data;

  Mux_2_1__5_bits mux_2_1_5_bits_1 (
    .Input_0(csr_control_signals_register_1_ad0), .Input_1(mapper_1_control_address),
    .Output(mux_2_1_5_bits_1_output), .Select(csr_control_signals_register_1_br));
  Mapper mapper_1 (.control_address(mapper_1_control_address), .opcode(CodeOp));
  // CAR_Control_Address_Register car_control_address_register_1: pin names not known; wires that end beside it: mux_2_1_5_bits_1_output, clk, car_control_address_register_1_p3, car_control_address_register_1_p4
  or or_1 (car_control_address_register_1_p3, M, ~csr_control_signals_register_1_cd);  // OR_Gate
  ROM #(.addrWidth(5), .dataWidth(17)) rom_1 (
    .addr(car_control_address_register_1_p4), .data(rom_1_data));  // open: sel
  not not_1 (not_1_out, clk);
  CSR_Control_Signals_Register csr_control_signals_register_1 (
    .\input (rom_1_data), .clk(not_1_out), .Write(1'b1), .AD0(csr_control_signals_register_1_ad0[0]),
    .AD1(csr_control_signals_register_1_ad0[1]), .AD3(csr_control_signals_register_1_ad0[3]),
    .AD2(csr_control_signals_register_1_ad0[2]), .MEMw(MEMw), .CD(csr_control_signals_register_1_cd),
    .BR(csr_control_signals_register_1_br), .AD4(csr_control_signals_register_1_ad0[4]), .RFw(DRw),
    .RFsrc(RFsrc), .DRsrc(DRsrc), .PC_plus_plus(PC_plus_plus), .IRw(IRw), .ARw(ARw), .DRw(DRw_2), .SRw(SRw),
    .RFxy(RFxy));

  // Notes on the sheet:
  //   Micro-code ROM
  //   contents of rom_1 (hex, n*v repeats v):
  //   c018 0 0 0 c018 0 0 0 10118 7*0 2211 8018 0 0 10215 98 0 0 819 101a 5c 20 41b
endmodule

module ALU (
  input  [2:0] Functions,
  input  [3:0] A,
  input  [3:0] B,
  output [3:0] Output,
  output zero,
  output negative,
  output overflow,
  output carry
);

  wire [3:0] adder_4_bits_1_sum, and_1_out, not_1_out, or_1_out, shifter_left_1_output,
       shifter_right_1_output, xor_1_out;
  wire [3:3] or_2_out;

  assign xor_1_out = {4{or_2_out[3]}} ^ B;  // XOR_Gate xor_1, 4 bits wide
  Adder_4_bits adder_4_bits_1 (
    .A(A), .B(xor_1_out), .Sum(adder_4_bits_1_sum), .Cin(or_2_out[3]), .Cout(carry), .overflow(overflow));
  assign and_1_out = A & B;  // AND_Gate and_1, 4 bits wide
  assign or_1_out = A | B;  // OR_Gate or_1, 4 bits wide
  assign not_1_out = ~A;  // NOT_Gate not_1, 4 bits wide
  Shifter_Left shifter_left_1 (.Input(A), .Output(shifter_left_1_output), .C1(1'b0), .C0(1'b1));
  Shifter_Right shifter_right_1 (.C1(1'b0), .C0(1'b1), .Input(A), .Output(shifter_right_1_output));
  or or_2 (or_2_out[3], Functions[2], Functions[1], Functions[0]);
  Mux_8_1__4_bits mux_8_1_4_bits_1 (
    .Input_0(adder_4_bits_1_sum), .Input_1(adder_4_bits_1_sum), .Input_2(and_1_out), .Input_3(or_1_out),
    .Input_4(adder_4_bits_1_sum), .Input_5(not_1_out), .Input_6(shifter_left_1_output),
    .Input_7(shifter_right_1_output), .Output({negative, Output[2:0]}), .Select_1(Functions[1]),
    .Select_0(Functions[0]), .Select_2(Functions[2]));
  nor nor_1 (zero, Output[0], Output[1], Output[2], negative);

  assign Output[3] = negative;
endmodule

// RF
module RF_Rgister_File__4x4_bits (
  input  clk,
  input  write,
  input  [1:0] dst,
  input  [1:0] X,
  input  [1:0] Y,
  input  [3:0] Input,
  output [3:0] X_output,
  output [3:0] Y_output
);

  wire and_1_out, and_2_out, and_3_out, and_4_out, decoder_2_4_1_out_3, decoder_2_4_1_out_4,
       decoder_2_4_1_out_5, decoder_2_4_1_out_6;
  wire [3:0] registre_4_bits_1_output, registre_4_bits_2_output, registre_4_bits_3_output,
       registre_4_bits_4_output;

  Decoder_2_4 decoder_2_4_1 (
    .Input_1(dst[1]), .Input_0(dst[0]), .out_3(decoder_2_4_1_out_3), .out_4(decoder_2_4_1_out_4),
    .out_5(decoder_2_4_1_out_5), .out_6(decoder_2_4_1_out_6));
  and and_1 (and_1_out, write, decoder_2_4_1_out_6);
  Registre_4_bits registre_4_bits_1 (
    .\input (Input), .\output (registre_4_bits_1_output), .clk(clk), .Write(and_1_out));
  and and_2 (and_2_out, write, decoder_2_4_1_out_5);
  Registre_4_bits registre_4_bits_2 (
    .\input (Input), .\output (registre_4_bits_2_output), .clk(clk), .Write(and_2_out));
  and and_3 (and_3_out, write, decoder_2_4_1_out_4);
  Registre_4_bits registre_4_bits_3 (
    .\input (Input), .\output (registre_4_bits_3_output), .clk(clk), .Write(and_3_out));
  and and_4 (and_4_out, write, decoder_2_4_1_out_3);
  Registre_4_bits registre_4_bits_4 (
    .\input (Input), .\output (registre_4_bits_4_output), .clk(clk), .Write(and_4_out));
  Mux_4_1__4_bits mux_4_1_4_bits_1 (
    .Input_0(registre_4_bits_1_output), .Input_1(registre_4_bits_2_output),
    .Input_2(registre_4_bits_3_output), .Input_3(registre_4_bits_4_output), .Output(X_output),
    .Select_0(X[0]), .Select_1(X[1]));
  Mux_4_1__4_bits mux_4_1_4_bits_2 (
    .Input_0(registre_4_bits_1_output), .Input_1(registre_4_bits_2_output),
    .Input_2(registre_4_bits_3_output), .Input_3(registre_4_bits_4_output), .Output(Y_output),
    .Select_0(Y[0]), .Select_1(Y[1]));
endmodule

// PC
module PC_Programe_Counter_Register (
  input  clk,
  input  count_enable,
  output [3:0] \output 
);

  Counter #(.width(4), .max('hf)) counter_1 (
    .count(count_enable), .Q(\output ), .clk(clk));  // open: load, D, carry, clr
endmodule

// IR
module Instruction_Register (
  input  clk,
  input  Write,
  input  [11:0] \input ,
  output _11,
  output _10,
  output _9,
  output _8,
  output _7,
  output _6,
  output _5,
  output _4,
  output _3,
  output _2,
  output _1,
  output _0
);

  D_Flip_Flop d_ff_1 (.clk(clk), .D(\input [0]), .Q(_0), .en(Write));  // open: Qn, preset, reset
  D_Flip_Flop d_ff_2 (.clk(clk), .D(\input [1]), .Q(_1), .en(Write));  // open: Qn, preset, reset
  D_Flip_Flop d_ff_3 (.clk(clk), .D(\input [2]), .Q(_2), .en(Write));  // open: Qn, preset, reset
  D_Flip_Flop d_ff_4 (.clk(clk), .D(\input [3]), .Q(_3), .en(Write));  // open: Qn, preset, reset
  D_Flip_Flop d_ff_5 (.clk(clk), .D(\input [4]), .Q(_4), .en(Write));  // open: Qn, preset, reset
  D_Flip_Flop d_ff_6 (.clk(clk), .D(\input [5]), .Q(_5), .en(Write));  // open: Qn, preset, reset
  D_Flip_Flop d_ff_7 (.clk(clk), .D(\input [6]), .Q(_6), .en(Write));  // open: Qn, preset, reset
  D_Flip_Flop d_ff_8 (.clk(clk), .D(\input [7]), .Q(_7), .en(Write));  // open: Qn, preset, reset
  D_Flip_Flop d_ff_9 (.clk(clk), .D(\input [8]), .Q(_8), .en(Write));  // open: Qn, preset, reset
  D_Flip_Flop d_ff_10 (.clk(clk), .D(\input [9]), .Q(_9), .en(Write));  // open: Qn, preset, reset
  D_Flip_Flop d_ff_11 (.clk(clk), .D(\input [10]), .Q(_10), .en(Write));  // open: Qn, preset, reset
  D_Flip_Flop d_ff_12 (.clk(clk), .D(\input [11]), .Q(_11), .en(Write));  // open: Qn, preset, reset
endmodule

// DR
module DR_Data_Register (
  input  clk,
  input  Write,
  input  [3:0] \input ,
  output [3:0] \output 
);

  D_Flip_Flop d_ff_1 (.clk(clk), .D(\input [0]), .Q(\output [0]), .en(Write));  // open: Qn, preset, reset
  D_Flip_Flop d_ff_2 (.clk(clk), .D(\input [1]), .Q(\output [1]), .en(Write));  // open: Qn, preset, reset
  D_Flip_Flop d_ff_3 (.clk(clk), .D(\input [2]), .Q(\output [2]), .en(Write));  // open: Qn, preset, reset
  D_Flip_Flop d_ff_4 (.clk(clk), .D(\input [3]), .Q(\output [3]), .en(Write));  // open: Qn, preset, reset
endmodule

// AR
module AR_Address_Register (
  input  clk,
  input  Write,
  input  [3:0] \input ,
  output [3:0] \output 
);

  D_Flip_Flop d_ff_1 (.clk(clk), .D(\input [0]), .Q(\output [0]), .en(Write));  // open: Qn, preset, reset
  D_Flip_Flop d_ff_2 (.clk(clk), .D(\input [1]), .Q(\output [1]), .en(Write));  // open: Qn, preset, reset
  D_Flip_Flop d_ff_3 (.clk(clk), .D(\input [2]), .Q(\output [2]), .en(Write));  // open: Qn, preset, reset
  D_Flip_Flop d_ff_4 (.clk(clk), .D(\input [3]), .Q(\output [3]), .en(Write));  // open: Qn, preset, reset
endmodule

// SR
module SR_Status_Register (
  input  clk,
  input  Write,
  input  [3:0] \input ,
  output [3:0] \output 
);

  D_Flip_Flop d_ff_1 (.clk(clk), .D(\input [0]), .Q(\output [0]), .en(Write));  // open: Qn, preset, reset
  D_Flip_Flop d_ff_2 (.clk(clk), .D(\input [1]), .Q(\output [1]), .en(Write));  // open: Qn, preset, reset
  D_Flip_Flop d_ff_3 (.clk(clk), .D(\input [2]), .Q(\output [2]), .en(Write));  // open: Qn, preset, reset
  D_Flip_Flop d_ff_4 (.clk(clk), .D(\input [3]), .Q(\output [3]), .en(Write));  // open: Qn, preset, reset
endmodule

// CAR
module CAR_Control_Address_Register (
  input  clk,
  input  Write,
  input  [4:0] in_3,
  output [4:0] out_4
);

  wire not_1_out;

  Counter #(.width(5), .max('h1f)) counter_1 (
    .load(Write), .D(in_3), .count(not_1_out), .Q(out_4), .clk(clk));  // open: carry, clr
  not not_1 (not_1_out, Write);
endmodule

// CSR
module CSR_Control_Signals_Register (
  input  clk,
  input  Write,
  input  [16:0] \input ,
  output RFxy,
  output RFsrc,
  output PC_plus_plus,
  output ARw,
  output SRw,
  output CD,
  output BR,
  output AD4,
  output AD3,
  output AD2,
  output AD1,
  output AD0,
  output RFw,
  output DRsrc,
  output IRw,
  output DRw,
  output MEMw
);

  D_Flip_Flop d_ff_1 (.clk(clk), .D(\input [0]), .Q(AD0), .en(Write));  // open: Qn, preset, reset
  D_Flip_Flop d_ff_2 (.clk(clk), .D(\input [1]), .Q(AD1), .en(Write));  // open: Qn, preset, reset
  D_Flip_Flop d_ff_3 (.clk(clk), .D(\input [2]), .Q(AD2), .en(Write));  // open: Qn, preset, reset
  D_Flip_Flop d_ff_4 (.clk(clk), .D(\input [3]), .Q(AD3), .en(Write));  // open: Qn, preset, reset
  D_Flip_Flop d_ff_5 (.clk(clk), .D(\input [4]), .Q(AD4), .en(Write));  // open: Qn, preset, reset
  D_Flip_Flop d_ff_6 (.clk(clk), .D(\input [5]), .Q(BR), .en(Write));  // open: Qn, preset, reset
  D_Flip_Flop d_ff_7 (.clk(clk), .D(\input [6]), .Q(CD), .en(Write));  // open: Qn, preset, reset
  D_Flip_Flop d_ff_8 (.clk(clk), .D(\input [7]), .Q(MEMw), .en(Write));  // open: Qn, preset, reset
  D_Flip_Flop d_ff_9 (.clk(clk), .D(\input [8]), .Q(SRw), .en(Write));  // open: Qn, preset, reset
  D_Flip_Flop d_ff_10 (.clk(clk), .D(\input [9]), .Q(DRw), .en(Write));  // open: Qn, preset, reset
  D_Flip_Flop d_ff_11 (.clk(clk), .D(\input [10]), .Q(ARw), .en(Write));  // open: Qn, preset, reset
  D_Flip_Flop d_ff_12 (.clk(clk), .D(\input [11]), .Q(IRw), .en(Write));  // open: Qn, preset, reset
  D_Flip_Flop d_ff_13 (.clk(clk), .D(\input [12]), .Q(PC_plus_plus), .en(Write));  // open: Qn, preset, reset
  D_Flip_Flop d_ff_14 (.clk(clk), .D(\input [13]), .Q(DRsrc), .en(Write));  // open: Qn, preset, reset
  D_Flip_Flop d_ff_15 (.clk(clk), .D(\input [14]), .Q(RFsrc), .en(Write));  // open: Qn, preset, reset
  D_Flip_Flop d_ff_16 (.clk(clk), .D(\input [15]), .Q(RFw), .en(Write));  // open: Qn, preset, reset
  D_Flip_Flop d_ff_17 (.clk(clk), .D(\input [16]), .Q(RFxy), .en(Write));  // open: Qn, preset, reset
endmodule

// <<
module Shifter_Left (
  input  C1,
  input  C0,
  input  [3:0] Input,
  output [3:0] Output
);

  Mux_4_1 mux_4_1_1 (
    .Input_0(Input[0]), .Input_1(1'b0), .Input_2(1'b0), .Input_3(1'b0), .Output(Output[0]), .Select_0(C0),
    .Select_1(C1));
  Mux_4_1 mux_4_1_2 (
    .Input_0(Input[1]), .Input_1(Input[0]), .Input_2(1'b0), .Input_3(1'b0), .Output(Output[1]),
    .Select_0(C0), .Select_1(C1));
  Mux_4_1 mux_4_1_3 (
    .Input_0(Input[2]), .Input_1(Input[1]), .Input_2(Input[0]), .Input_3(1'b0), .Output(Output[2]),
    .Select_0(C0), .Select_1(C1));
  Mux_4_1 mux_4_1_4 (
    .Input_0(Input[3]), .Input_1(Input[2]), .Input_2(Input[1]), .Input_3(Input[0]), .Output(Output[3]),
    .Select_0(C0), .Select_1(C1));
endmodule

// >>
module Shifter_Right (
  input  C1,
  input  C0,
  input  [3:0] Input,
  output [3:0] Output
);

  Mux_4_1 mux_4_1_1 (
    .Input_0(Input[0]), .Input_1(Input[1]), .Input_2(Input[2]), .Input_3(Input[3]), .Output(Output[0]),
    .Select_0(C0), .Select_1(C1));
  Mux_4_1 mux_4_1_2 (
    .Input_0(Input[1]), .Input_1(Input[2]), .Input_2(Input[3]), .Input_3(1'b0), .Output(Output[1]),
    .Select_0(C0), .Select_1(C1));
  Mux_4_1 mux_4_1_3 (
    .Input_0(Input[2]), .Input_1(Input[3]), .Input_2(1'b0), .Input_3(1'b0), .Output(Output[2]),
    .Select_0(C0), .Select_1(C1));
  Mux_4_1 mux_4_1_4 (
    .Input_0(Input[3]), .Input_1(1'b0), .Input_2(1'b0), .Input_3(1'b0), .Output(Output[3]), .Select_0(C0),
    .Select_1(C1));
endmodule

module Mapper (
  input  [3:0] opcode,
  output [4:0] control_address
);

  wire or_1_out, or_2_out;

  and and_1 (control_address[3], opcode[2], ~opcode[1], ~opcode[0]);  // AND_Gate
  or or_1 (or_1_out, opcode[3], opcode[2]);
  and and_2 (control_address[2], or_1_out, or_2_out);
  or or_2 (or_2_out, opcode[1], opcode[0]);

  assign {control_address[4], control_address[1:0]} = {opcode[3], 2'b00};
endmodule

module Registre_4_bits (
  input  clk,
  input  Write,
  input  [3:0] \input ,
  output [3:0] \output 
);

  D_Flip_Flop d_ff_1 (.clk(clk), .D(\input [0]), .Q(\output [0]), .en(Write));  // open: Qn, preset, reset
  D_Flip_Flop d_ff_2 (.clk(clk), .D(\input [1]), .Q(\output [1]), .en(Write));  // open: Qn, preset, reset
  D_Flip_Flop d_ff_3 (.clk(clk), .D(\input [2]), .Q(\output [2]), .en(Write));  // open: Qn, preset, reset
  D_Flip_Flop d_ff_4 (.clk(clk), .D(\input [3]), .Q(\output [3]), .en(Write));  // open: Qn, preset, reset
endmodule

module Adder_4_bits (
  input  Cin,
  input  [3:0] A,
  input  [3:0] B,
  output [3:0] Sum,
  output overflow,
  output Cout
);

  wire full_adder_1_cout, full_adder_2_cout, full_adder_3_cout;

  Full_Adder full_adder_1 (.A(A[0]), .B(B[0]), .S(Sum[0]), .Cin(Cin), .Cout(full_adder_1_cout));
  Full_Adder full_adder_2 (.A(A[1]), .B(B[1]), .S(Sum[1]), .Cin(full_adder_1_cout), .Cout(full_adder_2_cout));
  Full_Adder full_adder_3 (.A(A[2]), .B(B[2]), .S(Sum[2]), .Cin(full_adder_2_cout), .Cout(full_adder_3_cout));
  Full_Adder full_adder_4 (.A(A[3]), .B(B[3]), .S(Sum[3]), .Cin(full_adder_3_cout), .Cout(Cout));
  xor xor_1 (overflow, full_adder_3_cout, Cout);
endmodule

module Full_Adder (
  input  Cin,
  input  A,
  input  B,
  output S,
  output Cout
);

  wire and_1_out, and_2_out, and_3_out;

  xor xor_1 (S, A, B, Cin);
  and and_1 (and_1_out, A, B);
  and and_2 (and_2_out, A, Cin);
  and and_3 (and_3_out, B, Cin);
  or or_1 (Cout, and_1_out, and_2_out, and_3_out);
endmodule

module Mux_2_1 (
  input  Select,
  input  Input_0,
  input  Input_1,
  output Output
);

  wire and_1_out, and_2_out, not_1_out;

  not not_1 (not_1_out, Select);
  and and_1 (and_1_out, not_1_out, Input_0);
  and and_2 (and_2_out, Select, Input_1);
  or or_1 (Output, and_1_out, and_2_out);
endmodule

// Mux 2-1
module Mux_2_1__2_bits (
  input  Select,
  input  [1:0] Input_0,
  input  [1:0] Input_1,
  output [1:0] Output
);

  Mux_2_1 mux_2_1_1 (.Input_0(Input_0[0]), .Input_1(Input_1[0]), .Output(Output[0]), .Select(Select));
  Mux_2_1 mux_2_1_2 (.Input_0(Input_0[1]), .Input_1(Input_1[1]), .Output(Output[1]), .Select(Select));
endmodule

// Mux 2-1
module Mux_2_1__4_bits (
  input  Select,
  input  [3:0] Input_0,
  input  [3:0] Input_1,
  output [3:0] Output
);

  Mux_2_1 mux_2_1_1 (.Input_0(Input_0[0]), .Input_1(Input_1[0]), .Output(Output[0]), .Select(Select));
  Mux_2_1 mux_2_1_2 (.Input_0(Input_0[1]), .Input_1(Input_1[1]), .Output(Output[1]), .Select(Select));
  Mux_2_1 mux_2_1_3 (.Input_0(Input_0[2]), .Input_1(Input_1[2]), .Output(Output[2]), .Select(Select));
  Mux_2_1 mux_2_1_4 (.Input_0(Input_0[3]), .Input_1(Input_1[3]), .Output(Output[3]), .Select(Select));
endmodule

// Mux 2-1
module Mux_2_1__5_bits (
  input  Select,
  input  [4:0] Input_0,
  input  [4:0] Input_1,
  output [4:0] Output
);

  Mux_2_1 mux_2_1_1 (.Input_0(Input_0[0]), .Input_1(Input_1[0]), .Output(Output[0]), .Select(Select));
  Mux_2_1 mux_2_1_2 (.Input_0(Input_0[1]), .Input_1(Input_1[1]), .Output(Output[1]), .Select(Select));
  Mux_2_1 mux_2_1_3 (.Input_0(Input_0[2]), .Input_1(Input_1[2]), .Output(Output[2]), .Select(Select));
  Mux_2_1 mux_2_1_4 (.Input_0(Input_0[3]), .Input_1(Input_1[3]), .Output(Output[3]), .Select(Select));
  Mux_2_1 mux_2_1_5 (.Input_0(Input_0[4]), .Input_1(Input_1[4]), .Output(Output[4]), .Select(Select));
endmodule

module Mux_4_1 (
  input  Select_0,
  input  Select_1,
  input  Input_0,
  input  Input_1,
  input  Input_2,
  input  Input_3,
  output Output
);

  wire mux_2_1_1_output, mux_2_1_2_output;

  Mux_2_1 mux_2_1_1 (.Input_0(Input_0), .Input_1(Input_1), .Output(mux_2_1_1_output), .Select(Select_0));
  Mux_2_1 mux_2_1_2 (.Input_0(Input_2), .Input_1(Input_3), .Output(mux_2_1_2_output), .Select(Select_0));
  Mux_2_1 mux_2_1_3 (.Input_0(mux_2_1_1_output), .Input_1(mux_2_1_2_output), .Output(Output), .Select(Select_1));
endmodule

// Mux 4-1
module Mux_4_1__4_bits (
  input  Select_0,
  input  Select_1,
  input  [3:0] Input_0,
  input  [3:0] Input_1,
  input  [3:0] Input_2,
  input  [3:0] Input_3,
  output [3:0] Output
);

  wire [3:0] mux_2_1_4_bits_1_output, mux_2_1_4_bits_2_output;

  Mux_2_1__4_bits mux_2_1_4_bits_1 (
    .Input_0(Input_0), .Input_1(Input_1), .Output(mux_2_1_4_bits_1_output), .Select(Select_0));
  Mux_2_1__4_bits mux_2_1_4_bits_2 (
    .Input_0(Input_2), .Input_1(Input_3), .Output(mux_2_1_4_bits_2_output), .Select(Select_0));
  Mux_2_1__4_bits mux_2_1_4_bits_3 (
    .Input_0(mux_2_1_4_bits_1_output), .Input_1(mux_2_1_4_bits_2_output), .Output(Output), .Select(Select_1));
endmodule

// Mux 8-1
module Mux_8_1__4_bits (
  input  Select_1,
  input  Select_0,
  input  Select_2,
  input  [3:0] Input_0,
  input  [3:0] Input_1,
  input  [3:0] Input_2,
  input  [3:0] Input_3,
  input  [3:0] Input_4,
  input  [3:0] Input_5,
  input  [3:0] Input_6,
  input  [3:0] Input_7,
  output [3:0] Output
);

  wire [3:0] mux_4_1_4_bits_1_output, mux_4_1_4_bits_2_output;

  Mux_4_1__4_bits mux_4_1_4_bits_1 (
    .Input_0(Input_0), .Input_1(Input_1), .Input_2(Input_2), .Input_3(Input_3),
    .Output(mux_4_1_4_bits_1_output), .Select_0(Select_0), .Select_1(Select_1));
  Mux_4_1__4_bits mux_4_1_4_bits_2 (
    .Input_0(Input_4), .Input_1(Input_5), .Input_2(Input_6), .Input_3(Input_7),
    .Output(mux_4_1_4_bits_2_output), .Select_0(Select_0), .Select_1(Select_1));
  Mux_2_1__4_bits mux_2_1_4_bits_1 (
    .Input_0(mux_4_1_4_bits_1_output), .Input_1(mux_4_1_4_bits_2_output), .Output(Output), .Select(Select_2));
endmodule

module Decoder_2_4 (
  input  Input_1,
  input  Input_0,
  output out_3,
  output out_4,
  output out_5,
  output out_6
);

  wire not_1_out, not_2_out;

  not not_1 (not_1_out, Input_1);
  not not_2 (not_2_out, Input_0);
  and and_1 (out_6, not_2_out, not_1_out);
  and and_2 (out_5, Input_0, not_1_out);
  and and_3 (out_4, not_2_out, Input_1);
  and and_4 (out_3, Input_0, Input_1);
endmodule

module test (
  input  clk,
  input  M,
  input  [3:0] CodeOp,
  output DRw,
  output DRsrc,
  output IRw,
  output DRw_2,
  output MEMw,
  output RFxy,
  output RFsrc,
  output PC_plus_plus,
  output ARw,
  output SRw
);

  wire csr_control_signals_register_1_br, csr_control_signals_register_1_cd, not_1_out, or_1_out;
  wire [4:0] car_control_address_register_1_out_4, csr_control_signals_register_1_ad0,
       mapper_1_control_address, mux_2_1_5_bits_1_output;
  wire [16:0] rom_1_data;

  Mux_2_1__5_bits mux_2_1_5_bits_1 (
    .Input_0(csr_control_signals_register_1_ad0), .Input_1(mapper_1_control_address),
    .Output(mux_2_1_5_bits_1_output), .Select(csr_control_signals_register_1_br));
  Mapper mapper_1 (.control_address(mapper_1_control_address), .opcode(CodeOp));
  CAR_Control_Address_Register car_control_address_register_1 (
    .clk(clk), .Write(or_1_out), .out_4(car_control_address_register_1_out_4), .in_3(mux_2_1_5_bits_1_output));
  or or_1 (or_1_out, M, ~csr_control_signals_register_1_cd);  // OR_Gate
  ROM #(.addrWidth(5), .dataWidth(17)) rom_1 (
    .addr(car_control_address_register_1_out_4), .data(rom_1_data));  // open: sel
  not not_1 (not_1_out, clk);
  CSR_Control_Signals_Register csr_control_signals_register_1 (
    .\input (rom_1_data), .clk(not_1_out), .Write(1'b1), .AD0(csr_control_signals_register_1_ad0[0]),
    .AD1(csr_control_signals_register_1_ad0[1]), .AD3(csr_control_signals_register_1_ad0[3]),
    .AD2(csr_control_signals_register_1_ad0[2]), .MEMw(MEMw), .CD(csr_control_signals_register_1_cd),
    .BR(csr_control_signals_register_1_br), .AD4(csr_control_signals_register_1_ad0[4]), .RFw(DRw),
    .RFsrc(RFsrc), .DRsrc(DRsrc), .PC_plus_plus(PC_plus_plus), .IRw(IRw), .ARw(ARw), .DRw(DRw_2), .SRw(SRw),
    .RFxy(RFxy));

  // Notes on the sheet:
  //   Micro-code ROM
  //   contents of rom_1 (hex, n*v repeats v):
  //   c018 0 0 0 c018 0 0 0 10118 7*0 2211 8018 0 0 10215 98 0 0 819 101a 5c 20 41b
endmodule
